# Fritzing sketch sketch (saved by Fritzing 0.9.3b)
circuit board: 8.46667cm x 5.64444cm
breadboards: 1

parts:
  Mod1 = flyskyr6b
  J1 = Basic Servo
  IMU = MPU-6050 Board GY-521 [form="♀ (female)" package=THT]
  VL6181 = Adafruit VL6180X Time of Flight Distance Sensor [part_number="Adafruit #3316"]
  Part6 = Arduino Pro Mini v13
  M2 = ESC
  U1 = HALL-EFFECT [package=sc70]

nets:
  N1: Mod1.CH1, Part6.D9_PWM
  N2: Mod1.CH2, Part6.D8
  VCC: Mod1.VCC, Mod1.BAT+, J1.vcc, IMU.pin1, VL6181.VIN, Part6.VCC, M2.pin_8, U1.VCC
  GND: Mod1.connector14, Mod1.GND, J1.gnd, IMU.pin2, VL6181.GND, Part6.GND, M2.GND, U1.GND
  N3: J1.pulse, Part6.D7, U1.OUT
  N4: IMU.pin3, IMU.pin4, VL6181.SDA, Part6.D11_PWM/MOSI, Part6.D10_PWM/SS
  N5: Part6.D5_PWM, M2.DATA

custom parts:
  flyskyr6b: flysky r6b 6ch rc receiver module. Pcb view is 3*7 header pins, 3 female headers will let the board plug in to the receiver, or connect via wires as you choose.
  MPU-6050 Board GY-521: Acelerometro y Giroscopio MPU-6050 Board GY-521
  Adafruit VL6180X Time of Flight Distance Sensor: The VL6180X is a Time of Flight distance sensor like no other you've used! The sensor contains a very tiny invisible laser source, and a matching sensor. The VL6180X can detect the "time of flight", or how long the light has taken to bounce back to the sensor. Since it uses a very narrow light source, it is good for determining distance of only the surface directly in front of it. Unlike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
