# Fritzing sketch wlan_repeater_sketch (saved by Fritzing 0.9.3b)
circuit board: 8.46667cm x 5.64444cm

parts:
  Part6 = Arduino Pro Mini v13
  U1 = NodeMCU V1.0

nets:
  N1: Part6.D0/TX, U1.D7
  N2: Part6.D1/RX, U1.D8
  VCC: Part6.VCC, U1.Vin
  GND: Part6.GND, U1.GND
  N3: Part6.D11_PWM/MOSI, Part6.D10_PWM/SS

custom parts:
  NodeMCU V1.0: ESP8266 based NodeMCU
